# Fritzing sketch SmartPlant_basic_v1 (saved by Fritzing 0.9.2b)
circuit board: 8.46667cm x 5.64444cm
breadboards: 1

parts:
  Part1 = Arduino Uno (Rev3)
  Υγρασία = SoilWatch 10
  M1 = DC Motor
  Q1 = NPN-Transistor [package="TO92 [THT]"]
  D1 = Rectifier Diode [part_number=1N4001 package="300 mil [THT]"]
  LED1 = RGB LED (com. anode, rbg) [package="5 mm [THT]"]
  R1 = Resistor [tolerance=±5% resistance=10k package=THT]
  R2 = Resistor [tolerance=±5% resistance=680 package=THT]
  R3 = Resistor [tolerance=±5% resistance=680 package=THT]
  R4 = Resistor [tolerance=±5% resistance=680 package=THT]
  Στάθμη_Νερού = SoilWatch 10
  VCC1 = Battery block 9V

nets:
  N1: Part1.D8, R2.Pin_0
  N2: Part1.D9_PWM, R3.Pin_0
  N3: Part1.D10_PWM/SS, R4.Pin_0
  N4: Part1.D3_PWM, R1.Pin_0
  N5: Part1.D6_PWM, Υγρασία.OUT
  N6: Part1.D7, Στάθμη_Νερού.OUT
  VCC: Part1.5V, Υγρασία.VCC, M1.pin_1, D1.cathode, Στάθμη_Νερού.VCC
  GND: Part1.GND, Υγρασία.GND, Q1.E, LED1.common_anode, Στάθμη_Νερού.GND, VCC1.-
  N7: Part1.VIN, VCC1.+
  N8: M1.pin_2, Q1.C, D1.anode
  N9: Q1.B, R1.Pin_1
  N10: LED1.red_cathode, R4.Pin_1
  N11: LED1.blue_cathode, R3.Pin_1
  N12: LED1.green_cathode, R2.Pin_1

notes:
  Αισθητήρας στάθμης
  νερού
  Αισθητήρας υγρασίας
  Αντλία ποτίσματος

custom parts:
  SoilWatch 10: SoilWatch 10 - Capacitive soil moisture sensor
