# Fritzing sketch SmartPlant_schematics (saved by Fritzing 0.9.2b)
circuit board: 8.46667cm x 5.64444cm
breadboards: 1

parts:
  Part1 = Arduino Uno (Rev3)
  M1 = DC Motor
  Q1 = NPN-Transistor [package="TO92 [THT]"]
  D1 = Rectifier Diode [part_number=1N4001 package="300 mil [THT]"]
  LED1 = RGB LED (com. anode, rbg) [package="5 mm [THT]"]
  R1 = Resistor [tolerance=±5% resistance=10k package=THT]
  R2 = Resistor [tolerance=±5% resistance=680 package=THT]
  R3 = Resistor [tolerance=±5% resistance=680 package=THT]
  R4 = Resistor [tolerance=±5% resistance=680 package=THT]
  U1 = ESP8266 NodeMCU LoLin module
  PART1 = SparkFun Soil Moisture Sensor [part_number=SEN-13322]
  solar_cell1 = SOLAR-IXYS [package=solarbit-12x1]
  BAT1 = 18650 battery holder [package=battery-18650-kit]
  Water_Level_Sensor2 = Water Level Sensor
  Part3 = Power Cell LiPo Charger/Booster

nets:
  N1: Part1.A0, PART1.VCC
  N2: Part1.A1, PART1.SIG
  N3: Part1.A2, Water_Level_Sensor2.VCC
  N4: Part1.A3, Water_Level_Sensor2.SIG
  N5: Part1.A4/SDA, BAT1.+, Part3.VCC
  N6: Part1.D8, R2.Pin_0
  N7: Part1.D9_PWM, R3.Pin_0
  N8: Part1.D10_PWM/SS, R4.Pin_0
  N9: Part1.D13/SCK, U1.RST
  N10: Part1.D1/TX, U1.RX
  N11: Part1.D3_PWM, R1.Pin_0
  5V: Part1.5V, M1.pin_1, D1.cathode, U1.Vin
  GND: Part1.GND, Q1.E, LED1.common_anode, U1.GND, PART1.GND, solar_cell1.C, BAT1.-, Water_Level_Sensor2.GND, Part3.GND
  N12: Part1.VIN, Part3.VBATT
  N13: M1.pin_2, Q1.C, D1.anode
  N14: Q1.B, R1.Pin_1
  N15: LED1.red_cathode, R4.Pin_1
  N16: LED1.blue_cathode, R3.Pin_1
  N17: LED1.green_cathode, R2.Pin_1
  N18: solar_cell1.A, Part3.5VIN

notes:
  Αισθητήρας στάθμης
  νερού
  Αισθητήρας υγρασίας
  Αντλία ποτίσματος
  WiFi module
  Solar panel
  Μπαταρία
  Φορτιστής

custom parts:
  ESP8266 NodeMCU LoLin module: ESP8266 based NodeMCU
  SparkFun Soil Moisture Sensor: The SparkFun Soil Moisture Sensor is a simple breakout for measuring the moisture in soil and similar materials.
  18650 battery holder: 18650 Battery Holder
  Water Level Sensor: A water level sensor. This sensor operates at 3V to 5V. The Sig (signal) pin outputs an analogue signal that is in proportion to the amount of water in contact with the sensor.
